# Fritzing sketch synth-pants-fritzing (saved by Fritzing 1.0.2b)
breadboards: 1

parts:
  R1 = 220 Ω Resistor [package=THT]
  R2 = Resistor [tolerance=±5% resistance=1.5M package="2512 [SMD]"]
  Arduino_Uno = Arduino Uno (Rev3) - ICSP
  R4 = Resistor [tolerance=±5% resistance=47k package="2512 [SMD]"]
  R5 = Resistor [tolerance=±5% resistance=2.2k package="2512 [SMD]"]
  HC-06 = Bluetooth HC-05 Macho
  R6 = 220 Ω Resistor [package=THT]
  R9 = Resistor [tolerance=±5% resistance=1.5M package="2512 [SMD]"]
  R10 = Resistor [tolerance=±5% resistance=1.5M package="2512 [SMD]"]
  R11 = Resistor [tolerance=±5% resistance=1.5M package="2512 [SMD]"]

nets:
  N1: R1.330_Resistor, Arduino_Uno.A1
  GND: R1.Pin_1, Arduino_Uno.GND, R4.Pin_1, HC-06.GND, R6.Pin_1
  N2: R2.Pin_0, Arduino_Uno.D2
  5V: R2.Pin_1, Arduino_Uno.5V, HC-06.VCC, R9.Pin_1, R10.Pin_1, R11.Pin_1
  N3: Arduino_Uno.A2, R6.330_Resistor
  N4: Arduino_Uno.D8, R5.Pin_0
  N5: Arduino_Uno.D9_PWM, HC-06.RXD
  N6: Arduino_Uno.D3_PWM, R9.Pin_0
  N7: Arduino_Uno.D4, R10.Pin_0
  N8: Arduino_Uno.D5_PWM, R11.Pin_0
  N9: R4.Pin_0, R5.Pin_1, HC-06.TXD

notes:
  KNEE (A1)
  WALK (2)
  SIT (3)
  HC-06
  KNEE (A2)
  WALK (4)
  SIT (5)

custom parts:
  220 Ω Resistor: A generic resistor (0.25W)
